// Logisim project circuit.circ as structural Verilog: 14 circuits, main circuit main
module main (
  input  carry_in
);

  wire decoder_1_out0, decoder_1_out1, decoder_1_out2, decoder_1_out3, decoder_1_out4, decoder_1_out5,
       four_bit_full_adder_1_carry_out;
  wire [2:0] opcode_p3;
  wire [3:0] four_bit_full_adder_1_s0, four_bit_multiplier_1_s4, input_a_p4, input_b_p4;

  // DipSwitch #(.number(3)) opcode: pin names not known; wires that end beside it: opcode_p3[2], opcode_p3[1], opcode_p3[0]
  Decoder #(.enable("false"), .select(3)) decoder_1 (
    .out0(decoder_1_out0), .out1(decoder_1_out1), .out2(decoder_1_out2), .out3(decoder_1_out3),
    .out4(decoder_1_out4), .out5(decoder_1_out5), .sel(opcode_p3));  // open: out6, out7
  Hex_Digit_Display hex_digit_display_1 (.value({1'b0, opcode_p3}));  // open: dp
  // DipSwitch #(.number(4)) input_a: pin names not known; wires that end beside it: input_a_p4[3], input_a_p4[2], input_a_p4[1], input_a_p4[0]
  Hex_Digit_Display hex_digit_display_2 (.value(input_a_p4));  // open: dp
  // DipSwitch #(.number(4)) input_b: pin names not known; wires that end beside it: input_b_p4[3], input_b_p4[2], input_b_p4[1], input_b_p4[0]
  Hex_Digit_Display hex_digit_display_3 (.value(input_b_p4));  // open: dp
  LED led_1 (.in(carry_in));
  Hex_Digit_Display hex_digit_display_4 (.value(four_bit_multiplier_1_s4));  // open: dp
  Hex_Digit_Display hex_digit_display_5 (.value(four_bit_full_adder_1_s0));  // open: dp
  LED carry_out (.in(four_bit_full_adder_1_carry_out));
  four_bit_full_adder four_bit_full_adder_1 (
    .enable(decoder_1_out0), .a0(input_a_p4[0]), .b0(input_b_p4[0]), .carry_in(carry_in), .a1(input_a_p4[1]),
    .b1(input_b_p4[1]), .a2(input_a_p4[2]), .b2(input_b_p4[2]), .a3(input_a_p4[3]), .b3(input_b_p4[3]),
    .s0(four_bit_full_adder_1_s0[0]), .s1(four_bit_full_adder_1_s0[1]), .s2(four_bit_full_adder_1_s0[2]),
    .s3(four_bit_full_adder_1_s0[3]), .carry_out(four_bit_full_adder_1_carry_out));
  four_bit_full_subtractor four_bit_full_subtractor_1 (
    .enable(decoder_1_out1), .a0(input_a_p4[0]), .b0(input_b_p4[0]), .borrow_in(carry_in),
    .a1(input_a_p4[1]), .b1(input_b_p4[1]), .a2(input_a_p4[2]), .b2(input_b_p4[2]), .a3(input_a_p4[3]),
    .b3(input_b_p4[3]), .s0(four_bit_full_adder_1_s0[0]), .s1(four_bit_full_adder_1_s0[1]),
    .s2(four_bit_full_adder_1_s0[2]), .s3(four_bit_full_adder_1_s0[3]),
    .borrow_out(four_bit_full_adder_1_carry_out));
  four_bit_multiplier four_bit_multiplier_1 (
    .enable(decoder_1_out2), .a0(input_a_p4[0]), .a1(input_a_p4[1]), .a2(input_a_p4[2]), .a3(input_a_p4[3]),
    .b0(input_b_p4[0]), .b1(input_b_p4[1]), .b2(input_b_p4[2]), .b3(input_b_p4[3]),
    .s0(four_bit_full_adder_1_s0[0]), .s1(four_bit_full_adder_1_s0[1]), .s2(four_bit_full_adder_1_s0[2]),
    .s3(four_bit_full_adder_1_s0[3]), .s4(four_bit_multiplier_1_s4[0]), .s5(four_bit_multiplier_1_s4[1]),
    .s6(four_bit_multiplier_1_s4[2]), .s7(four_bit_multiplier_1_s4[3]));
  four_bit_and four_bit_and_1 (
    .a0(input_a_p4[0]), .enable(decoder_1_out3), .b0(input_b_p4[0]), .a1(input_a_p4[1]), .b1(input_b_p4[1]),
    .a2(input_a_p4[2]), .b2(input_b_p4[2]), .a3(input_a_p4[3]), .b3(input_b_p4[3]),
    .s0(four_bit_full_adder_1_s0[0]), .s1(four_bit_full_adder_1_s0[1]), .s2(four_bit_full_adder_1_s0[2]),
    .s3(four_bit_full_adder_1_s0[3]));
  four_bit_or four_bit_or_1 (
    .a0(input_a_p4[0]), .enable(decoder_1_out4), .b0(input_b_p4[0]), .a1(input_a_p4[1]), .b1(input_b_p4[1]),
    .a2(input_a_p4[2]), .b2(input_b_p4[2]), .a3(input_a_p4[3]), .b3(input_b_p4[3]),
    .s0(four_bit_full_adder_1_s0[0]), .s1(four_bit_full_adder_1_s0[1]), .s2(four_bit_full_adder_1_s0[2]),
    .s3(four_bit_full_adder_1_s0[3]));
  four_bit_xor four_bit_xor_1 (
    .a0(input_a_p4[0]), .enable(decoder_1_out5), .b0(input_b_p4[0]), .a1(input_a_p4[1]), .b1(input_b_p4[1]),
    .a2(input_a_p4[2]), .b2(input_b_p4[2]), .a3(input_a_p4[3]), .b3(input_b_p4[3]),
    .s0(four_bit_full_adder_1_s0[0]), .s1(four_bit_full_adder_1_s0[1]), .s2(four_bit_full_adder_1_s0[2]),
    .s3(four_bit_full_adder_1_s0[3]));
endmodule

module four_bit_and (
  input  a0,
  input  enable,
  input  b0,
  input  a1,
  input  b1,
  input  a2,
  input  b2,
  input  a3,
  input  b3,
  output s0,
  output s1,
  output s2,
  output s3
);

  wire and_1_out, and_2_out, and_3_out, and_4_out;

  and and_1 (and_1_out, a0, b0);
  and and_2 (and_2_out, a1, b1);
  and and_3 (and_3_out, a2, b2);
  and and_4 (and_4_out, a3, b3);
  one_bit_switch one_bit_switch_1 (.a(and_1_out), .s(enable), .b(s0));
  one_bit_switch one_bit_switch_2 (.a(and_2_out), .s(enable), .b(s1));
  one_bit_switch one_bit_switch_3 (.a(and_3_out), .s(enable), .b(s2));
  one_bit_switch one_bit_switch_4 (.a(and_4_out), .s(enable), .b(s3));
endmodule

module four_bit_or (
  input  a0,
  input  enable,
  input  b0,
  input  a1,
  input  b1,
  input  a2,
  input  b2,
  input  a3,
  input  b3,
  output s0,
  output s1,
  output s2,
  output s3
);

  wire or_1_out, or_2_out, or_3_out, or_4_out;

  or or_1 (or_1_out, a0, b0);
  or or_2 (or_2_out, a1, b1);
  or or_3 (or_3_out, a2, b2);
  or or_4 (or_4_out, a3, b3);
  one_bit_switch one_bit_switch_1 (.a(or_1_out), .s(enable), .b(s0));
  one_bit_switch one_bit_switch_2 (.a(or_2_out), .s(enable), .b(s1));
  one_bit_switch one_bit_switch_3 (.a(or_3_out), .s(enable), .b(s2));
  one_bit_switch one_bit_switch_4 (.a(or_4_out), .s(enable), .b(s3));
endmodule

module four_bit_xor (
  input  a0,
  input  enable,
  input  b0,
  input  a1,
  input  b1,
  input  a2,
  input  b2,
  input  a3,
  input  b3,
  output s0,
  output s1,
  output s2,
  output s3
);

  wire xor_1_out, xor_2_out, xor_3_out, xor_4_out;

  xor xor_1 (xor_1_out, a0, b0);
  xor xor_2 (xor_2_out, a1, b1);
  xor xor_3 (xor_3_out, a2, b2);
  xor xor_4 (xor_4_out, a3, b3);
  one_bit_switch one_bit_switch_1 (.a(xor_1_out), .s(enable), .b(s0));
  one_bit_switch one_bit_switch_2 (.a(xor_2_out), .s(enable), .b(s1));
  one_bit_switch one_bit_switch_3 (.a(xor_3_out), .s(enable), .b(s2));
  one_bit_switch one_bit_switch_4 (.a(xor_4_out), .s(enable), .b(s3));
endmodule

module one_bit_switch (
  input  a,
  input  s,
  output b
);

  Multiplexer multiplexer_1 (.in1(a), .out(b), .sel(s));  // open: in0
endmodule

module four_bit_full_adder (
  input  enable,
  input  a0,
  input  b0,
  input  carry_in,
  input  a1,
  input  b1,
  input  a2,
  input  b2,
  input  a3,
  input  b3,
  output s0,
  output s1,
  output s2,
  output s3,
  output carry_out
);

  wire one_bit_full_adder_1_carry_out, one_bit_full_adder_1_s, one_bit_full_adder_2_carry_out,
       one_bit_full_adder_2_s, one_bit_full_adder_3_carry_out, one_bit_full_adder_3_s,
       one_bit_full_adder_4_carry_out, one_bit_full_adder_4_s;

  one_bit_full_adder one_bit_full_adder_1 (
    .a(a0), .b(b0), .carry_in(carry_in), .s(one_bit_full_adder_1_s),
    .carry_out(one_bit_full_adder_1_carry_out));
  one_bit_full_adder one_bit_full_adder_2 (
    .a(a1), .b(b1), .carry_in(one_bit_full_adder_1_carry_out), .s(one_bit_full_adder_2_s),
    .carry_out(one_bit_full_adder_2_carry_out));
  one_bit_full_adder one_bit_full_adder_3 (
    .a(a2), .b(b2), .carry_in(one_bit_full_adder_2_carry_out), .s(one_bit_full_adder_3_s),
    .carry_out(one_bit_full_adder_3_carry_out));
  one_bit_full_adder one_bit_full_adder_4 (
    .a(a3), .b(b3), .carry_in(one_bit_full_adder_3_carry_out), .s(one_bit_full_adder_4_s),
    .carry_out(one_bit_full_adder_4_carry_out));
  one_bit_switch one_bit_switch_1 (.a(one_bit_full_adder_1_s), .s(enable), .b(s0));
  one_bit_switch one_bit_switch_2 (.a(one_bit_full_adder_2_s), .s(enable), .b(s1));
  one_bit_switch one_bit_switch_3 (.a(one_bit_full_adder_3_s), .s(enable), .b(s2));
  one_bit_switch one_bit_switch_4 (.a(one_bit_full_adder_4_s), .s(enable), .b(s3));
  one_bit_switch one_bit_switch_5 (.a(one_bit_full_adder_4_carry_out), .s(enable), .b(carry_out));
endmodule

module four_bit_full_subtractor (
  input  enable,
  input  a0,
  input  b0,
  input  borrow_in,
  input  a1,
  input  b1,
  input  a2,
  input  b2,
  input  a3,
  input  b3,
  output s0,
  output s1,
  output s2,
  output s3,
  output borrow_out
);

  wire one_bit_full_subtractor_1_borrow_out, one_bit_full_subtractor_1_s,
       one_bit_full_subtractor_2_borrow_out, one_bit_full_subtractor_2_s,
       one_bit_full_subtractor_3_borrow_out, one_bit_full_subtractor_3_s,
       one_bit_full_subtractor_4_borrow_out, one_bit_full_subtractor_4_s;

  one_bit_full_subtractor one_bit_full_subtractor_1 (
    .a(a0), .b(b0), .borrow_in(borrow_in), .s(one_bit_full_subtractor_1_s),
    .borrow_out(one_bit_full_subtractor_1_borrow_out));
  one_bit_full_subtractor one_bit_full_subtractor_2 (
    .a(a1), .b(b1), .borrow_in(one_bit_full_subtractor_1_borrow_out), .s(one_bit_full_subtractor_2_s),
    .borrow_out(one_bit_full_subtractor_2_borrow_out));
  one_bit_full_subtractor one_bit_full_subtractor_3 (
    .a(a2), .b(b2), .borrow_in(one_bit_full_subtractor_2_borrow_out), .s(one_bit_full_subtractor_3_s),
    .borrow_out(one_bit_full_subtractor_3_borrow_out));
  one_bit_full_subtractor one_bit_full_subtractor_4 (
    .a(a3), .b(b3), .borrow_in(one_bit_full_subtractor_3_borrow_out), .s(one_bit_full_subtractor_4_s),
    .borrow_out(one_bit_full_subtractor_4_borrow_out));
  one_bit_switch one_bit_switch_1 (.a(one_bit_full_subtractor_1_s), .s(enable), .b(s0));
  one_bit_switch one_bit_switch_2 (.a(one_bit_full_subtractor_2_s), .s(enable), .b(s1));
  one_bit_switch one_bit_switch_3 (.a(one_bit_full_subtractor_3_s), .s(enable), .b(s2));
  one_bit_switch one_bit_switch_4 (.a(one_bit_full_subtractor_4_s), .s(enable), .b(s3));
  one_bit_switch one_bit_switch_5 (.a(one_bit_full_subtractor_4_borrow_out), .s(enable), .b(borrow_out));
endmodule

module one_bit_full_adder (
  input  a,
  input  b,
  input  carry_in,
  output s,
  output carry_out
);

  wire and_1_out, and_2_out, xor_1_out;

  xor xor_1 (xor_1_out, a, b);
  and and_1 (and_1_out, a, b);
  and and_2 (and_2_out, xor_1_out, carry_in);
  xor xor_2 (s, xor_1_out, carry_in);
  or or_1 (carry_out, and_2_out, and_1_out);
endmodule

module one_bit_full_subtractor (
  input  a,
  input  b,
  input  borrow_in,
  output s,
  output borrow_out
);

  wire and_1_out, and_2_out, not_1_out, not_2_out, xor_1_out;

  xor xor_1 (xor_1_out, a, b);
  not not_1 (not_1_out, a);
  xor xor_2 (s, xor_1_out, borrow_in);
  not not_2 (not_2_out, xor_1_out);
  and and_1 (and_1_out, not_1_out, b);
  and and_2 (and_2_out, borrow_in, not_2_out);
  or or_1 (borrow_out, and_2_out, and_1_out);
endmodule

module one_bit_half_adder (
  input  a,
  input  b,
  output s,
  output carry_out
);

  xor xor_1 (s, a, b);
  and and_1 (carry_out, a, b);
endmodule

module two_bit_full_adder (
  input  a0,
  input  b0,
  input  carry_in,
  input  a1,
  input  b1,
  output s0,
  output s1,
  output carry_out
);

  wire one_bit_full_adder_1_carry_out;

  one_bit_full_adder one_bit_full_adder_1 (
    .a(a0), .b(b0), .carry_in(carry_in), .s(s0), .carry_out(one_bit_full_adder_1_carry_out));
  one_bit_full_adder one_bit_full_adder_2 (
    .a(a1), .b(b1), .carry_in(one_bit_full_adder_1_carry_out), .s(s1), .carry_out(carry_out));
endmodule

module three_bit_full_adder (
  input  a0,
  input  b0,
  input  carry_in,
  input  a1,
  input  b1,
  input  a2,
  input  b2,
  output s0,
  output s1,
  output s2,
  output carry_out
);

  wire one_bit_full_adder_1_carry_out;

  one_bit_full_adder one_bit_full_adder_1 (
    .a(a0), .b(b0), .carry_in(carry_in), .s(s0), .carry_out(one_bit_full_adder_1_carry_out));
  two_bit_full_adder two_bit_full_adder_1 (
    .a0(a1), .b0(b1), .carry_in(one_bit_full_adder_1_carry_out), .a1(a2), .b1(b2), .s0(s1), .s1(s2),
    .carry_out(carry_out));
endmodule

module four_bit_multiplier (
  input  enable,
  input  a0,
  input  a1,
  input  a2,
  input  a3,
  input  b0,
  input  b1,
  input  b2,
  input  b3,
  output s0,
  output s1,
  output s2,
  output s3,
  output s4,
  output s5,
  output s6,
  output s7
);

  wire a0b0_out, a0b1_out, a0b2_out, a0b3_out, a1b0_out, a1b1_out, a1b2_out, a1b3_out, a2b0_out, a2b1_out,
       a2b2_out, a2b3_out, a3b0_out, a3b1_out, a3b2_out, a3b3_out, one_bit_half_adder_1_carry_out,
       one_bit_half_adder_1_s, one_bit_half_adder_2_carry_out, one_bit_half_adder_2_s,
       one_bit_half_adder_3_carry_out, one_bit_half_adder_3_s, one_bit_half_adder_4_carry_out,
       one_bit_half_adder_4_s, three_bit_full_adder_1_carry_out, three_bit_full_adder_1_s0,
       three_bit_full_adder_1_s1, three_bit_full_adder_1_s2, three_bit_full_adder_2_carry_out,
       three_bit_full_adder_2_s0, three_bit_full_adder_2_s1, three_bit_full_adder_2_s2,
       two_bit_full_adder_1_carry_out, two_bit_full_adder_1_s0, two_bit_full_adder_1_s1;

  and a0b0 (a0b0_out, a0, b0);
  and a1b0 (a1b0_out, a1, b0);
  and a2b0 (a2b0_out, a2, b0);
  and a3b0 (a3b0_out, a3, b0);
  and a0b1 (a0b1_out, a0, b1);
  and a1b1 (a1b1_out, a1, b1);
  and a2b1 (a2b1_out, a2, b1);
  and a3b1 (a3b1_out, a3, b1);
  one_bit_half_adder one_bit_half_adder_1 (
    .a(a1b0_out), .b(a0b1_out), .s(one_bit_half_adder_1_s), .carry_out(one_bit_half_adder_1_carry_out));
  two_bit_full_adder two_bit_full_adder_1 (
    .a0(a2b0_out), .b0(a1b1_out), .carry_in(one_bit_half_adder_1_carry_out), .a1(a3b0_out), .b1(a2b1_out),
    .s0(two_bit_full_adder_1_s0), .s1(two_bit_full_adder_1_s1), .carry_out(two_bit_full_adder_1_carry_out));
  one_bit_half_adder one_bit_half_adder_2 (
    .a(two_bit_full_adder_1_carry_out), .b(a3b1_out), .s(one_bit_half_adder_2_s),
    .carry_out(one_bit_half_adder_2_carry_out));
  and a0b2 (a0b2_out, a0, b2);
  and a1b2 (a1b2_out, a1, b2);
  and a2b2 (a2b2_out, a2, b2);
  and a3b2 (a3b2_out, a3, b2);
  one_bit_half_adder one_bit_half_adder_3 (
    .a(two_bit_full_adder_1_s0), .b(a0b2_out), .s(one_bit_half_adder_3_s),
    .carry_out(one_bit_half_adder_3_carry_out));
  three_bit_full_adder three_bit_full_adder_1 (
    .a0(a1b2_out), .b0(two_bit_full_adder_1_s1), .carry_in(one_bit_half_adder_3_carry_out), .a1(a2b2_out),
    .b1(one_bit_half_adder_2_s), .a2(one_bit_half_adder_2_carry_out), .b2(a3b2_out),
    .s0(three_bit_full_adder_1_s0), .s1(three_bit_full_adder_1_s1), .s2(three_bit_full_adder_1_s2),
    .carry_out(three_bit_full_adder_1_carry_out));
  and a0b3 (a0b3_out, a0, b3);
  and a1b3 (a1b3_out, a1, b3);
  and a2b3 (a2b3_out, a2, b3);
  and a3b3 (a3b3_out, a3, b3);
  one_bit_half_adder one_bit_half_adder_4 (
    .a(a0b3_out), .b(three_bit_full_adder_1_s0), .s(one_bit_half_adder_4_s),
    .carry_out(one_bit_half_adder_4_carry_out));
  three_bit_full_adder three_bit_full_adder_2 (
    .a0(a1b3_out), .b0(three_bit_full_adder_1_s1), .carry_in(one_bit_half_adder_4_carry_out), .a1(a2b3_out),
    .b1(three_bit_full_adder_1_s2), .a2(three_bit_full_adder_1_carry_out), .b2(a3b3_out),
    .s0(three_bit_full_adder_2_s0), .s1(three_bit_full_adder_2_s1), .s2(three_bit_full_adder_2_s2),
    .carry_out(three_bit_full_adder_2_carry_out));
  one_bit_switch one_bit_switch_1 (.a(a0b0_out), .s(enable), .b(s0));
  one_bit_switch one_bit_switch_2 (.a(one_bit_half_adder_1_s), .s(enable), .b(s1));
  one_bit_switch one_bit_switch_3 (.a(one_bit_half_adder_3_s), .s(enable), .b(s2));
  one_bit_switch one_bit_switch_4 (.a(one_bit_half_adder_4_s), .s(enable), .b(s3));
  one_bit_switch_and one_bit_switch_and_1 (.a(three_bit_full_adder_2_s0), .s(enable), .b(s4));
  one_bit_switch_and one_bit_switch_and_2 (.a(three_bit_full_adder_2_s1), .s(enable), .b(s5));
  one_bit_switch_and one_bit_switch_and_3 (.a(three_bit_full_adder_2_s2), .s(enable), .b(s6));
  one_bit_switch_and one_bit_switch_and_4 (.a(three_bit_full_adder_2_carry_out), .s(enable), .b(s7));
endmodule

module one_bit_switch_and (
  input  a,
  input  s,
  output b
);

  and and_1 (b, a, s);
endmodule
